# Fritzing sketch helloprotoswith (saved by Fritzing 0.8.3b)
breadboards: 1

parts:
  Part1 = Arduino Uno (Rev3)
  R1 = Resistor [tolerance=±5% resistance=220 package=THT]
  LED1 = LED - 5mm [color="Red (633nm)" package="5 mm [THT]"]
  S1 = Pushbutton [package="[THT]"]

nets:
  N1: Part1.GND, R1.Pin_0
  N2: R1.Pin_1, LED1.cathode
  N3: LED1.anode, S1.Pin_1, S1.Pin_2, S1.Pin_3, S1.Pin_4
